// Logisim project Mux.circ as structural Verilog: 1 circuit, main circuit Mux 4_1 c/ 2 3 Mux 2_1
module Mux_4_1_c__2_3_Mux_2_1 (
  input  in_1,
  input  in_2,
  input  in_3,
  input  in_4,
  input  in_5,
  input  in_6,
  output out_7
);

  wire and_1_out, and_2_out, and_3_out, and_4_out, and_5_out, and_6_out, not_1_out, not_2_out, not_3_out,
       or_1_out, or_2_out;

  not not_1 (not_1_out, in_3);
  not not_2 (not_2_out, in_3);
  and and_1 (and_1_out, in_1, in_1, not_1_out);
  and and_2 (and_2_out, in_3, in_2);
  and and_3 (and_3_out, in_5, in_5, not_2_out);
  and and_4 (and_4_out, in_3, in_6);
  or or_1 (or_1_out, and_1_out, and_2_out);
  or or_2 (or_2_out, and_3_out, and_4_out);
  not not_3 (not_3_out, in_4);
  and and_5 (and_5_out, or_1_out, or_1_out, not_3_out);
  and and_6 (and_6_out, in_4, or_2_out);
  or or_3 (out_7, and_5_out, and_6_out);
endmodule
